// Logisim project Ch7.circ as structural Verilog
module main (
);

  wire AluInAClk, AluInBClk, AluOutClk, InsRegClk, MemClk, MemInClk, MemOutClk, MemSelClk,
       n5_bit_register_1_p2, OpCodeClk, ParamClk, RegAClk, RegBClk, RegCClk, RegClk, RegInClk, RegOutClk,
       RegSelClk, undriven_2;
  wire [2:0] multiplexer_2_out, n3_bit_register_1_output, n3_bit_register_2_output, n3_bit_register_3_output,
       n3_bit_register_4_output, n3_bit_register_5_output, n16_bit_register_6_output;
  wire [7:0] n8_bit_register_1_output;
  wire [15:0] carry_in_1_out, Memory_data_out, multiplexer_1_out, n16_bit_alu_1_result,
       n16_bit_register_1_output, n16_bit_register_2_output, n16_bit_register_3_output,
       n16_bit_register_4_output, n16_bit_register_5_output, n16_bit_register_7_output, Registers_data_out,
       undriven, undriven_3;
  wire [15:3] n16_bit_register_6_output_2;

  Control_Logic Control_Logic ();
  Instruction_Register Instruction_Register (.In(n16_bit_register_7_output), .Out(undriven), .Clock(InsRegClk));
  // _5_bit_register 5_bit_register_1: pin names not known; wires that end beside it: OpCodeClk, n5_bit_register_1_p2, undriven[15:11]
  _16_bit_register u_16_bit_register_1 (
    .Clock(AluInAClk), .Input({n16_bit_register_6_output_2, n16_bit_register_6_output}),
    .Output(n16_bit_register_1_output), .Clock_2(undriven_2));
  _16_bit_register u_16_bit_register_2 (
    .Clock(undriven_2), .Input({n16_bit_register_6_output_2, n16_bit_register_6_output}),
    .Output(n16_bit_register_2_output), .Clock_2(AluInBClk));
  _3_bit_register u_3_bit_register_1 (
    .Input(undriven[10:8]), .Output(n3_bit_register_1_output), .Clock_2(RegAClk));  // open: Clock
  _3_bit_register u_3_bit_register_2 (
    .Input(undriven[7:5]), .Output(n3_bit_register_2_output), .Clock_2(RegBClk));  // open: Clock
  _3_bit_register u_3_bit_register_3 (
    .Input(undriven[4:2]), .Output(n3_bit_register_3_output), .Clock_2(RegCClk));  // open: Clock
  _16_bit_register u_16_bit_register_3 (
    .Input(n16_bit_alu_1_result), .Output(n16_bit_register_3_output), .Clock_2(AluOutClk));  // open: Clock
  _16_BIT_ALU u_16_bit_alu_1 (
    .A(n16_bit_register_1_output), .B(n16_bit_register_2_output), .Result(n16_bit_alu_1_result));  // open: Invert_A, Invert_B, Operation, CarryOut_Overflow
  _8_bit_register u_8_bit_register_1 (
    .Input(undriven[7:0]), .Output(n8_bit_register_1_output), .Clock_2(ParamClk));  // open: Clock
  Multiplexer #(.select(2), .width(16)) multiplexer_1 (
    .in0({{8{1'b0}}, n8_bit_register_1_output}), .in1(n16_bit_register_7_output),
    .in2(n16_bit_register_3_output), .in3(carry_in_1_out), .out(multiplexer_1_out));  // open: sel, en
  Carry_In carry_in_1 (
    .IN({n16_bit_register_6_output_2, n16_bit_register_6_output}), .Out(carry_in_1_out));  // open: Carry_In
  Multiplexer #(.select(2), .width(3)) multiplexer_2 (
    .in0(n3_bit_register_1_output), .in1(n3_bit_register_2_output), .in2(n3_bit_register_3_output),
    .out(multiplexer_2_out));  // open: in3, sel, en
  _16_bit_register u_16_bit_register_4 (
    .Clock(RegInClk), .Input(multiplexer_1_out), .Output(n16_bit_register_4_output));  // open: Clock_2
  _16_bit_register u_16_bit_register_5 (
    .Clock(MemInClk), .Input(undriven_3), .Output(n16_bit_register_5_output));  // open: Clock_2
  _3_bit_register u_3_bit_register_4 (
    .Input(multiplexer_2_out), .Output(n3_bit_register_4_output), .Clock(RegSelClk));  // open: Clock_2
  _16_bit_8_word_register Registers (
    .Data_In(n16_bit_register_4_output), .Clock(RegClk), .Data_Out(Registers_data_out),
    .Select_In(n3_bit_register_4_output));
  _3_bit_register u_3_bit_register_5 (
    .Input(n16_bit_register_6_output), .Output(n3_bit_register_5_output), .Clock(MemSelClk));  // open: Clock_2
  _16_bit_8_word_register Memory (
    .Data_In(n16_bit_register_5_output), .Clock(MemClk), .Data_Out(Memory_data_out),
    .Select_In(n3_bit_register_5_output));
  _16_bit_register u_16_bit_register_6 (
    .Clock(RegOutClk), .Input(Registers_data_out),
    .Output({n16_bit_register_6_output_2, n16_bit_register_6_output}));  // open: Clock_2
  _16_bit_register u_16_bit_register_7 (
    .Clock(MemOutClk), .Input(Memory_data_out), .Output(n16_bit_register_7_output));  // open: Clock_2
endmodule

module Control_Logic (
);

  wire InsRegClk;

  Clock clock_1 (.out(InsRegClk));

  // Other names for the same wires on the sheet: OpCodeClk = InsRegClk; ParamClk = InsRegClk; RegAClk = InsRegClk;
  //   RegBClk = InsRegClk; RegCClk = InsRegClk
endmodule

// 3
module _3_bit_register (
  input  Clock,
  input  [2:0] Input,
  input  Clock_2,
  output [2:0] Output
);

  D_Flip_Flop d_ff_1 (.clk(Clock), .D(Input[0]), .Q(Output[0]));  // open: Qn, preset, en, reset
  D_Flip_Flop d_ff_2 (.clk(Clock), .D(Input[1]), .Q(Output[1]));  // open: Qn, preset, en, reset
  D_Flip_Flop d_ff_3 (.clk(Clock), .D(Input[2]), .Q(Output[2]));  // open: Qn, preset, en, reset

  assign Clock_2 = Clock;
endmodule

// 5
module _5_bit_register (
  input  Clock,
  input  [4:0] Input,
  output [4:0] Output
);

  D_Flip_Flop d_ff_1 (.clk(Clock), .D(Input[0]), .Q(Output[0]));  // open: Qn, preset, en, reset
  D_Flip_Flop d_ff_2 (.clk(Clock), .D(Input[1]), .Q(Output[1]));  // open: Qn, preset, en, reset
  D_Flip_Flop d_ff_3 (.clk(Clock), .D(Input[2]), .Q(Output[2]));  // open: Qn, preset, en, reset
  D_Flip_Flop d_ff_4 (.clk(Clock), .D(Input[3]), .Q(Output[3]));  // open: Qn, preset, en, reset
  D_Flip_Flop d_ff_5 (.clk(Clock), .D(Input[4]), .Q(Output[4]));  // open: Qn, preset, en, reset
endmodule

// 8
module _8_bit_register (
  input  Clock,
  input  [7:0] Input,
  input  Clock_2,
  output [7:0] Output
);

  D_Flip_Flop d_ff_1 (.clk(Clock), .D(Input[0]), .Q(Output[0]));  // open: Qn, preset, en, reset
  D_Flip_Flop d_ff_2 (.clk(Clock), .D(Input[1]), .Q(Output[1]));  // open: Qn, preset, en, reset
  D_Flip_Flop d_ff_3 (.clk(Clock), .D(Input[2]), .Q(Output[2]));  // open: Qn, preset, en, reset
  D_Flip_Flop d_ff_4 (.clk(Clock), .D(Input[3]), .Q(Output[3]));  // open: Qn, preset, en, reset
  D_Flip_Flop d_ff_5 (.clk(Clock), .D(Input[4]), .Q(Output[4]));  // open: Qn, preset, en, reset
  D_Flip_Flop d_ff_6 (.clk(Clock), .D(Input[5]), .Q(Output[5]));  // open: Qn, preset, en, reset
  D_Flip_Flop d_ff_7 (.clk(Clock), .D(Input[6]), .Q(Output[6]));  // open: Qn, preset, en, reset
  D_Flip_Flop d_ff_8 (.clk(Clock), .D(Input[7]), .Q(Output[7]));  // open: Qn, preset, en, reset

  assign Clock_2 = Clock;
endmodule

// 16
module _16_bit_register (
  input  Clock,
  input  [15:0] Input,
  input  Clock_2,
  output [15:0] Output
);

  D_Flip_Flop d_ff_1 (.clk(Clock), .D(Input[14]), .Q(Output[14]));  // open: Qn, preset, en, reset
  D_Flip_Flop d_ff_2 (.clk(Clock), .D(Input[6]), .Q(Output[6]));  // open: Qn, preset, en, reset
  D_Flip_Flop d_ff_3 (.clk(Clock), .D(Input[8]), .Q(Output[8]));  // open: Qn, preset, en, reset
  D_Flip_Flop d_ff_4 (.clk(Clock), .D(Input[10]), .Q(Output[10]));  // open: Qn, preset, en, reset
  D_Flip_Flop d_ff_5 (.clk(Clock), .D(Input[12]), .Q(Output[12]));  // open: Qn, preset, en, reset
  D_Flip_Flop d_ff_6 (.clk(Clock), .D(Input[13]), .Q(Output[13]));  // open: Qn, preset, en, reset
  D_Flip_Flop d_ff_7 (.clk(Clock), .D(Input[15]), .Q(Output[15]));  // open: Qn, preset, en, reset
  D_Flip_Flop d_ff_8 (.clk(Clock), .D(Input[0]), .Q(Output[0]));  // open: Qn, preset, en, reset
  D_Flip_Flop d_ff_9 (.clk(Clock), .D(Input[2]), .Q(Output[2]));  // open: Qn, preset, en, reset
  D_Flip_Flop d_ff_10 (.clk(Clock), .D(Input[4]), .Q(Output[4]));  // open: Qn, preset, en, reset
  D_Flip_Flop d_ff_11 (.clk(Clock), .D(Input[5]), .Q(Output[5]));  // open: Qn, preset, en, reset
  D_Flip_Flop d_ff_12 (.clk(Clock), .D(Input[7]), .Q(Output[7]));  // open: Qn, preset, en, reset
  D_Flip_Flop d_ff_13 (.clk(Clock), .D(Input[9]), .Q(Output[9]));  // open: Qn, preset, en, reset
  D_Flip_Flop d_ff_14 (.clk(Clock), .D(Input[11]), .Q(Output[11]));  // open: Qn, preset, en, reset
  D_Flip_Flop d_ff_15 (.clk(Clock), .D(Input[1]), .Q(Output[1]));  // open: Qn, preset, en, reset
  D_Flip_Flop d_ff_16 (.clk(Clock), .D(Input[3]), .Q(Output[3]));  // open: Qn, preset, en, reset

  assign Clock_2 = Clock;
endmodule

module Instruction_Register (
  input  [15:0] In,
  input  [15:0] Out,
  input  Clock
);
endmodule

module Carry_In (
  input  [15:0] IN,
  input  Carry_In,
  output [15:0] Out
);

  _16_bit_adder__bundled_i_o u_16_bit_adder_bundled_i_o_1 (
    .CarryIn(Carry_In), .A(IN), .B({16{1'b0}}), .Out(Out));  // open: CarryOut

  // Notes on the sheet:
  //   Out: pull=down
endmodule
